# Fritzing sketch DarknessSensorBreadboard (saved by Fritzing 0.9.3b)
breadboards: 1

parts:
  VCC1 = Battery block 9V
  LED1 = LED - 5mm [color="Red (633nm)" package="5 mm [THT]"]
  R4 = PHOTOCELL [package=photocell]
  IC1 = IC, DIP package, 8 pins [chip_label=LM393]
  R6 = Resistor [tolerance=±5% resistance=3k package=THT]
  R3 = Resistor [tolerance=±5% resistance=15k package=THT]
  R1 = Resistor [tolerance=±5% resistance=1k package=THT]
  R2 = Resistor [tolerance=±5% resistance=1k package=THT]

nets:
  N1: VCC1.-, LED1.cathode, R4.P$1, IC1.pin4, R2.Pin_0
  N2: VCC1.+, IC1.pin8, R6.Pin_1, R3.Pin_1, R1.Pin_1
  N3: LED1.anode, IC1.pin1, R6.Pin_0
  N4: R4.P$2, IC1.pin3, R3.Pin_0
  N5: IC1.pin2, R1.Pin_0, R2.Pin_1
