# Fritzing sketch LM7805Breadboard (saved by Fritzing 0.9.3b)
breadboards: 1

parts:
  IC1 = Voltage Regulator [part_number=7805 package=to220-igo]
  VCC1 = Battery block 9V

nets:
  N1: IC1.GND, VCC1.+
  N2: IC1.IN, VCC1.-
