# Fritzing sketch ParallelUsingBreadboard (saved by Fritzing 0.9.3b)
breadboards: 1

parts:
  VCC1 = Battery block 9V
  R1 = Resistor [tolerance=±5% resistance=200 package=THT]
  LED1 = LED - 5mm [color="Red (633nm)" package="5 mm [THT]"]
  LED2 = LED - 5mm [color="Red (633nm)" package="5 mm [THT]"]
  R2 = Resistor [tolerance=±5% resistance=200 package=THT]
  R3 = Resistor [tolerance=±5% resistance=200 package=THT]

nets:
  N1: VCC1.-, R2.Pin_1, R3.Pin_1
  N2: VCC1.+, R1.Pin_0
  N3: R1.Pin_1, LED1.anode, LED2.anode
  N4: LED1.cathode, R3.Pin_0
  N5: LED2.cathode, R2.Pin_0
