# Fritzing sketch Simple555OscillatorBreadboard (saved by Fritzing 0.9.3b)
breadboards: 1

parts:
  VCC1 = Battery block 9V
  U1 = 555 Timer [package="DIP8 [THT]"]
  R2 = Resistor [tolerance=±5% resistance=50k package=THT]
  R1 = Resistor [tolerance=±5% resistance=50 package=THT]
  C1 = Electrolytic Capacitor [capacitance=10µF package="100 mil [THT, electrolytic]"]
  LED1 = LED - 5mm [color="Red (633nm)" package="5 mm [THT]"]
  C2 = Electrolytic Capacitor [capacitance=1µF package="100 mil [THT, electrolytic]"]
  R3 = Resistor [tolerance=±5% resistance=1k package=THT]

nets:
  N1: VCC1.-, U1.Ground, C1.-, LED1.cathode, C2.-
  N2: VCC1.+, U1.Reset, U1.Vcc_Supply_Voltage, R1.Pin_1
  N3: U1.Trigger, U1.Threshold, R2.Pin_0, C1.+
  N4: U1.Output, R3.Pin_0
  N5: U1.Control_Voltage, C2.+
  N6: U1.Discharge, R2.Pin_1, R1.Pin_0
  N7: LED1.anode, R3.Pin_1
