# Fritzing sketch SimpleTimerBreadboard (saved by Fritzing 0.9.3b)
breadboards: 1

parts:
  VCC1 = Battery block 9V
  R1 = Resistor [tolerance=±5% resistance=1k package=THT]
  LED1 = LED - 5mm [color="Red (633nm)" package="5 mm [THT]"]
  R2 = Resistor [tolerance=±5% resistance=68k package=THT]
  R3 = Resistor [tolerance=±5% resistance=10k package=THT]
  R4 = Resistor [tolerance=±5% resistance=10k package=THT]
  C4 = Electrolytic Capacitor [capacitance=100µF package="0405 [SMD, electrolytic]"]
  U1 = IC, DIP package, 8 pins [chip_label=LM393]

nets:
  N1: VCC1.-, LED1.cathode, R4.Pin_1, C4.-, U1.pin4
  N2: VCC1.+, R1.Pin_0, R2.Pin_1, R3.Pin_1, U1.pin8
  N3: R1.Pin_1, LED1.anode, U1.pin7
  N4: R2.Pin_0, C4.+, U1.pin5
  N5: R3.Pin_0, R4.Pin_0, U1.pin6
