# Fritzing sketch SimpleToneGeneratorBreadboard (saved by Fritzing 0.9.3b)
breadboards: 1

parts:
  VCC1 = Battery block 9V
  U1 = 555 Timer [package="DIP8 [THT]"]
  R2 = Resistor [tolerance=±5% resistance=10k package=THT]
  R1 = Resistor [tolerance=±5% resistance=10 package=THT]
  C2 = Electrolytic Capacitor [capacitance=1µF package="100 mil [THT, electrolytic]"]
  R3 = Resistor [tolerance=±5% resistance=150 package=THT]
  TRS1 = Audio Jack (TRS) 3.5mm [package="PG203J [THT]"]
  C3 = Electrolytic Capacitor [capacitance=10µF package="100 mil [THT, electrolytic]"]
  C4 = Ceramic Capacitor [capacitance=100nF package="100 mil [THT, multilayer]"]

nets:
  N1: VCC1.-, U1.Ground, C2.-, TRS1.Sleeve, C4.0
  N2: VCC1.+, U1.Reset, U1.Vcc_Supply_Voltage, R1.Pin_1
  N3: U1.Trigger, U1.Threshold, R2.Pin_0, C4.1
  N4: U1.Output, C3.+
  N5: U1.Control_Voltage, C2.+
  N6: U1.Discharge, R2.Pin_1, R1.Pin_0
  N7: R3.Pin_0, C3.-
  N8: R3.Pin_1, TRS1.Tip
