# Fritzing sketch TwoStageAmplifierBuild (saved by Fritzing 0.9.3b)
breadboards: 1

parts:
  YwRobot_Power_Supply1 = YwRobot Breadboard Power Supply 5V [part_number=545043]
  TRS1 = Audio Jack (TRS) 3.5mm [package="PG203J [THT]"]
  C1 = Electrolytic Capacitor [capacitance=1µF package="100 mil [THT, electrolytic]"]
  R1 = Resistor [tolerance=±5% resistance=47k package=THT]
  R2 = Resistor [tolerance=±5% resistance=10k package=THT]
  Q1 = NPN-Transistor [package="TO92 [THT]"]
  R3 = Resistor [tolerance=±5% resistance=100 package=THT]
  C2 = Capacitor [package=cap-pth-small2]
  R5 = Resistor [tolerance=±5% resistance=2.2k package=THT]
  R6 = Resistor [tolerance=±5% resistance=47k package=THT]
  R7 = Resistor [tolerance=±5% resistance=10k package=THT]
  Q2 = NPN-Transistor [package="TO92 [THT]"]
  R8 = Resistor [tolerance=±5% resistance=100 package=THT]
  R9 = Resistor [tolerance=±5% resistance=2.2k package=THT]
  TRS2 = Audio Jack (TRS) 3.5mm [package="PG203J [THT]"]
  C3 = Electrolytic Capacitor [capacitance=1µF package="100 mil [THT, electrolytic]"]
  R10 = Resistor [tolerance=±5% resistance=10 package=THT]
  R11 = Resistor [tolerance=±5% resistance=1M package=THT]
  R12 = Resistor [tolerance=±5% resistance=1M package=THT]

nets:
  N1: YwRobot_Power_Supply1.VCC#5, YwRobot_Power_Supply1.VCC#6, R9.Pin_0
  N2: YwRobot_Power_Supply1.VCC#9, YwRobot_Power_Supply1.VCC#10, R1.Pin_1, R5.Pin_1, R6.Pin_1
  N3: YwRobot_Power_Supply1.GND#11, YwRobot_Power_Supply1.GND#12, TRS1.Sleeve, R8.Pin_1, R11.Pin_0, R12.Pin_0
  N4: YwRobot_Power_Supply1.GND#13, YwRobot_Power_Supply1.GND#14, R2.Pin_1, R3.Pin_1, R7.Pin_1, TRS2.Sleeve
  N5: TRS1.Tip, C1.-, R12.Pin_1
  N6: C1.+, R1.Pin_0, R2.Pin_0, Q1.B
  N7: Q1.E, R3.Pin_0
  N8: Q1.C, C2.1, R5.Pin_0
  N9: C2.2, R6.Pin_0, R7.Pin_0, Q2.B
  N10: Q2.E, R8.Pin_0
  N11: Q2.C, R9.Pin_1, C3.+
  N12: TRS2.Ring, TRS2.Tip, R10.Pin_1, R11.Pin_1
  N13: C3.-, R10.Pin_0

notes:
  Plug microphone here
  Plug headphones here

custom parts:
  YwRobot Breadboard Power Supply 5V: The YwRobot Breadboard Power Supply (MB-V2) has two power rails; they can be 5V or 3V3 (this variant is 5V only). Power to the module can be provided through the female USB socket or through the A10 (female) 2.1mm power jack.
  Capacitor: Capacitor Standard 0603 ceramic capacitor, and 0.1 leaded capacitor.
